# Fritzing sketch esquema (saved by Fritzing 0.9.3b)
breadboards: 1

parts:
  Componente1 = Arduino Uno (Rev3)
  Componente2 = Bluetooth HC-05 Macho
  R1 = Resistor [tolerance=±5% resistance=330 package=THT]
  R2 = Resistor [tolerance=±5% resistance=330 package=THT]
  R3 = Resistor [tolerance=±5% resistance=10k package=THT]
  J1 = Basic Servo
  R4 = Photocell (LDR) [package=THT]

nets:
  N1: Componente1.A0, R3.Pin_0, R4.pin_1
  N2: Componente1.D9_PWM, J1.pulse
  GND: Componente1.GND, Componente2.GND, R2.Pin_0, R3.Pin_1, J1.gnd
  N3: Componente1.D0/RX, Componente2.TXD
  N4: Componente1.D1/TX, R1.Pin_1
  VCC: Componente1.5V, Componente2.VCC, J1.vcc, R4.pin_0
  N5: Componente2.RXD, R1.Pin_0, R2.Pin_1
